# Fritzing sketch 2.2.4_PIR (saved by Fritzing 0.9.3b)
breadboards: 1

parts:
  T-Cobbler1 = GPIO Extension Board
  S1 = PIR2 [package=THT]
  LED1 = LED - 5mm [color="Red (633nm)" package="5 mm [THT]"]
  R1 = Resistor [tolerance=±5% resistance=220 package=THT]

nets:
  3V3: T-Cobbler1.3V3, S1.VCC
  N1: T-Cobbler1.GND#4, S1.GND, R1.Pin_1
  N2: T-Cobbler1.#17, S1.OUT
  N3: T-Cobbler1.#18, LED1.anode
  N4: LED1.cathode, R1.Pin_0

custom parts:
  GPIO Extension Board: T-Cobbler for RPi B+ and Rpi2 from SunFounder
